# Fritzing sketch M02_Deneyap_6-EksenAtaletselOlcumBirimi (saved by Fritzing 0.9.10b)
breadboards: 1

parts:
  IC1 = IC, DIP package, 6 pins [chip_label=IC]  # not connected
  Deneyap_Kart1 = Deneyap 6-Eksenli Ataletsel Ölçüm Birimi [package="DIP (Dual Inline) [THT]"]
  Deneyap_Kart2 = Deneyap 6-Eksenli Ataletsel Ölçüm Birimi [package="DIP (Dual Inline) [THT]"]

nets:
  N1: Deneyap_Kart1.3V3, Deneyap_Kart1.INT1, Deneyap_Kart1.INT2
  N2: Deneyap_Kart1.SDA, Deneyap_Kart1.GND
  N3: Deneyap_Kart2.INT1, Deneyap_Kart2.INT2

custom parts:
  Deneyap 6-Eksenli Ataletsel Ölçüm Birimi: Ülkemizin mühendislik kaynakları kullanılarak geliştirilen Deneyap Mini; güçlü işlemcisi, dayanıklı tasarımı ve çok yönlü giriş/çıkış pinleri ile kullanıcılara Elektronik Programlama, Nesnelerin İnterneti (IoT) ve Yapay Zeka alanlarında başlangıç seviyesinden endüstriyel uygulamalara kadar her seviyede projeyi yapma imkanı sunuyor.
