# Fritzing sketch M37_Deneyap_DokunmatikTusTakimi (saved by Fritzing 0.9.10b)
breadboards: 1

parts:
  IC1 = IC, DIP package, 16 pins [chip_label=IC]  # not connected
  Deneyap_Kart1 = Deneyap Kart Dokunmatik Tuş Takımı [package="DIP (Dual Inline) [THT]"]

nets:
  N1: Deneyap_Kart1.BUT0, Deneyap_Kart1.BUT2, Deneyap_Kart1.BUT4, Deneyap_Kart1.BUT6, Deneyap_Kart1.BUT7
  N2: Deneyap_Kart1.BUT5, Deneyap_Kart1.BUT3, Deneyap_Kart1.BUT1, Deneyap_Kart1.SCL, Deneyap_Kart1.SDA

custom parts:
  Deneyap Kart Dokunmatik Tuş Takımı: Ülkemizin mühendislik kaynakları kullanılarak geliştirilen Deneyap Kart Dokunmatik Tuş Takımı; güçlü işlemcisi, dayanıklı tasarımı ve çok yönlü giriş/çıkış pinleri ile kullanıcılara Elektronik Programlama, Nesnelerin İnterneti (IoT) ve Yapay Zeka alanlarında başlangıç seviyesinden endüstriyel uygulamalara kadar her seviyede projeyi yapma imkanı sunuyor.
