# Fritzing sketch M47_Deneyap_9-EksenAtaletselOlcumBirimi (saved by Fritzing 0.9.10b)
breadboards: 1

parts:
  IC1 = IC, DIP package, 6 pins [chip_label=IC]  # not connected
  Deneyap_Kart1 = Deneyap Kart 9-Eksen Ataletsel Ölçüm Birimi [package="DIP (Dual Inline) [THT]"]

nets:
  N1: Deneyap_Kart1.3V3, Deneyap_Kart1.INT1, Deneyap_Kart1.INT2
  N2: Deneyap_Kart1.SCL, Deneyap_Kart1.SDA, Deneyap_Kart1.GND

custom parts:
  Deneyap Kart 9-Eksen Ataletsel Ölçüm Birimi: Ülkemizin mühendislik kaynakları kullanılarak geliştirilen Deneyap Mini; güçlü işlemcisi, dayanıklı tasarımı ve çok yönlü giriş/çıkış pinleri ile kullanıcılara Elektronik Programlama, Nesnelerin İnterneti (IoT) ve Yapay Zeka alanlarında başlangıç seviyesinden endüstriyel uygulamalara kadar her seviyede projeyi yapma imkanı sunuyor.
