# Fritzing sketch M59_Deneyap_HareketAlgilama (saved by Fritzing 0.9.10b)
breadboards: 1

parts:
  IC1 = IC, DIP package, 8 pins [chip_label=IC]  # not connected
  Deneyap_Kart1 = Deneyap Kart Hareket Algılama [package="DIP (Dual Inline) [THT]"]

nets:
  N1: Deneyap_Kart1.3V3, Deneyap_Kart1.OUT, Deneyap_Kart1.RES, Deneyap_Kart1.AOUT
  N2: Deneyap_Kart1.SWIM, Deneyap_Kart1.SCL, Deneyap_Kart1.SDA, Deneyap_Kart1.GND

custom parts:
  Deneyap Kart Hareket Algılama: Ülkemizin mühendislik kaynakları kullanılarak geliştirilen Deneyap Kart Hareket Algılama; güçlü işlemcisi, dayanıklı tasarımı ve çok yönlü giriş/çıkış pinleri ile kullanıcılara Elektronik Programlama, Nesnelerin İnterneti (IoT) ve Yapay Zeka alanlarında başlangıç seviyesinden endüstriyel uygulamalara kadar her seviyede projeyi yapma imkanı sunuyor.
